// Logisim project Digital Vending Machine.circ as structural Verilog: 4 circuits, main circuit Digital Vending Machine
module Digital_Vending_Machine (
);

  wire _1_out, _2_out, _5_out, _10_out, _20_out, _50_out, _100_out, Cancel_out;

  Button _1 (.out(_1_out));
  Button _2 (.out(_2_out));
  Button _5 (.out(_5_out));
  Button _10 (.out(_10_out));
  Button _20 (.out(_20_out));
  Button _50 (.out(_50_out));
  Button _100 (.out(_100_out));
  Button Cancel (.out(Cancel_out));
  Insert_Money insert_money_1 (
    ._1(_1_out), ._2(_2_out), ._5(_5_out), ._10(_10_out), .Clear(Cancel_out));  // open: out_6, out_7, out_8, out_9
endmodule

module Insert_Money (
  input  Clear,
  input  _1,
  input  _2,
  input  _5,
  input  _10,
  output out_6,
  output out_7,
  output out_8,
  output out_9
);

  wire adder_1_cout, adder_1_out, adder_2_cout, adder_2_out, adder_3_cout, adder_3_out, adder_4_cout,
       adder_4_out, LSB_out, nor_1_out, or_1_out;

  or or_1 (or_1_out, _10, _2);
  or LSB (LSB_out, _5, _1);
  nor nor_1 (nor_1_out, adder_1_cout, _10, _5, _2, _1);
  Adder #(.width(1)) adder_1 (.a(out_6), .b(_10), .out(adder_1_out), .cin(adder_2_cout), .cout(adder_1_cout));
  Adder #(.width(1)) adder_2 (.a(out_7), .b(_5), .out(adder_2_out), .cin(adder_3_cout), .cout(adder_2_cout));
  Adder #(.width(1)) adder_3 (.a(out_8), .b(or_1_out), .out(adder_3_out), .cin(adder_4_cout), .cout(adder_3_cout));
  Adder #(.width(1)) adder_4 (.a(out_9), .b(LSB_out), .out(adder_4_out), .cout(adder_4_cout));  // open: cin
  D_Flip_Flop d_ff_1 (.clk(nor_1_out), .D(adder_1_out), .Q(out_6), .reset(Clear));  // open: Qn, preset, en
  D_Flip_Flop d_ff_2 (.clk(nor_1_out), .D(adder_2_out), .Q(out_7), .reset(Clear));  // open: Qn, preset, en
  D_Flip_Flop d_ff_3 (.clk(nor_1_out), .D(adder_3_out), .Q(out_8), .reset(Clear));  // open: Qn, preset, en
  D_Flip_Flop d_ff_4 (.clk(nor_1_out), .D(adder_4_out), .Q(out_9), .reset(Clear));  // open: Qn, preset, en
endmodule

module _8_bit_binary_to_7_segment_display (
  input  in_1,
  input  in_2,
  input  in_3,
  input  in_4,
  input  in_5,
  input  in_6,
  input  in_7,
  input  in_8
);
endmodule

module Profuct_Selection (
  input  _2,
  input  _5,
  input  _10,
  input  _25,
  input  _60,
  input  _120,
  input  _220
);

  // OR_Gate or_1 is placed but not wired
  // OR_Gate or_2 is placed but not wired
  // OR_Gate or_3 has open pins: in0=_220, in1=_120, in2=_60, in3=_25, in4=_10, out=open
  // OR_Gate or_4 has open pins: in0=_220, in1=_60, in2=_5, out=open
  // OR_Gate or_5 has open pins: in0=_10, in1=_2, out=open
  // OR_Gate LSB has open pins: in0=_25, in1=_5, out=open
endmodule
